// Logisim project Lucas_de_Souza_Cerveira_Pereira.circ as structural Verilog: 12 circuits, main circuit main
module somador_1bit (
  input  c_in,
  input  a,
  input  b,
  output out_4,
  output out_5
);

  wire and_1_out, and_2_out, and_3_out, xor_1_out;

  xor xor_1 (xor_1_out, a, b);
  xor xor_2 (out_4, xor_1_out, c_in);
  and and_1 (and_1_out, a, c_in);
  and and_2 (and_2_out, a, b);
  and and_3 (and_3_out, b, c_in);
  or or_1 (out_5, and_1_out, and_2_out, and_3_out);
endmodule

module main (
  input  in_1,
  input  [7:0] in_2,
  input  in_3,
  input  in_4,
  input  in_5,
  input  in_6,
  input  in_7,
  input  in_8,
  input  in_9,
  input  in_10,
  input  in_11,
  input  in_12,
  input  in_13,
  input  in_14
);

  wire or_1_out;
  wire [7:0] controlled_buffer_1_out, ram_1_dout, register_1_q;

  assign controlled_buffer_1_out = in_14 ? ram_1_dout : 8'bz;  // Controlled_Buffer controlled_buffer_1
  assign controlled_buffer_1_out = in_3 ? in_2 : 8'bz;  // Controlled_Buffer controlled_buffer_2
  registradorsetenable registradorsetenable_1 (
    .in_1(controlled_buffer_1_out), .in_2(in_5), .in_3(in_10), .out_4(controlled_buffer_1_out));
  registradorsetenable registradorsetenable_2 (
    .in_1(controlled_buffer_1_out), .in_2(in_6), .in_3(in_8), .out_4(controlled_buffer_1_out));
  // Probe on ram_1_dout
  registradorsetenable registradorsetenable_3 (
    .in_1(controlled_buffer_1_out), .in_2(in_4), .in_3(in_7), .out_4(controlled_buffer_1_out));
  registradorsetenable registradorsetenable_4 (
    .in_1(controlled_buffer_1_out), .in_2(in_9), .in_3(in_11), .out_4(controlled_buffer_1_out));
  or or_1 (or_1_out, in_12, in_13);
  Register register_1 (.D(controlled_buffer_1_out), .Q(register_1_q), .clk(in_1));  // open: en, clr
  RAM ram_1 (
    .addr(register_1_q), .we(in_12), .oe(in_13), .clk(or_1_out), .din(controlled_buffer_1_out),
    .dout(ram_1_dout));

  // Notes on the sheet:
  //   Lucas de Souza Cerveira Pereira - 22401904
endmodule

module somador_8bit (
  input  in_1,
  input  [7:0] in_2,
  input  [7:0] in_3,
  output [7:0] out_4,
  output out_5
);

  wire somador_1bit_1_out_5, somador_1bit_2_out_5, somador_1bit_3_out_5, somador_1bit_4_out_5,
       somador_1bit_5_out_5, somador_1bit_6_out_5, somador_1bit_7_out_5;

  somador_1bit somador_1bit_1 (.a(in_2[0]), .b(in_3[0]), .c_in(in_1), .out_4(out_4[0]), .out_5(somador_1bit_1_out_5));
  somador_1bit somador_1bit_2 (
    .a(in_2[1]), .b(in_3[1]), .c_in(somador_1bit_1_out_5), .out_4(out_4[1]), .out_5(somador_1bit_2_out_5));
  somador_1bit somador_1bit_3 (
    .a(in_2[2]), .b(in_3[2]), .c_in(somador_1bit_2_out_5), .out_4(out_4[2]), .out_5(somador_1bit_3_out_5));
  somador_1bit somador_1bit_4 (
    .a(in_2[3]), .b(in_3[3]), .c_in(somador_1bit_3_out_5), .out_4(out_4[3]), .out_5(somador_1bit_4_out_5));
  somador_1bit somador_1bit_5 (
    .a(in_2[4]), .b(in_3[4]), .c_in(somador_1bit_4_out_5), .out_4(out_4[4]), .out_5(somador_1bit_5_out_5));
  somador_1bit somador_1bit_6 (
    .a(in_2[5]), .b(in_3[5]), .c_in(somador_1bit_5_out_5), .out_4(out_4[5]), .out_5(somador_1bit_6_out_5));
  somador_1bit somador_1bit_7 (
    .a(in_2[6]), .b(in_3[6]), .c_in(somador_1bit_6_out_5), .out_4(out_4[6]), .out_5(somador_1bit_7_out_5));
  somador_1bit somador_1bit_8 (.a(in_2[7]), .b(in_3[7]), .c_in(somador_1bit_7_out_5), .out_4(out_4[7]), .out_5(out_5));
endmodule

module memory_1bit (
  input  in_1,
  input  in_2,
  output out_3
);

  wire nand_1_out, nand_2_out, nand_4_out;

  nand nand_1 (nand_1_out, in_1, in_2);
  nand nand_2 (nand_2_out, in_2, nand_1_out);
  nand nand_3 (out_3, nand_1_out, nand_4_out);
  nand nand_4 (nand_4_out, out_3, nand_2_out);
endmodule

module registrador (
  input  [7:0] in_1,
  input  in_2,
  output [7:0] out_3
);

  memory_1bit memory_1bit_1 (.in_1(in_1[0]), .in_2(in_2), .out_3(out_3[0]));
  memory_1bit memory_1bit_2 (.in_1(in_1[1]), .in_2(in_2), .out_3(out_3[1]));
  memory_1bit memory_1bit_3 (.in_1(in_1[2]), .in_2(in_2), .out_3(out_3[2]));
  memory_1bit memory_1bit_4 (.in_1(in_1[3]), .in_2(in_2), .out_3(out_3[3]));
  memory_1bit memory_1bit_5 (.in_1(in_1[4]), .in_2(in_2), .out_3(out_3[4]));
  memory_1bit memory_1bit_6 (.in_1(in_1[5]), .in_2(in_2), .out_3(out_3[5]));
  memory_1bit memory_1bit_7 (.in_1(in_1[6]), .in_2(in_2), .out_3(out_3[6]));
  memory_1bit memory_1bit_8 (.in_1(in_1[7]), .in_2(in_2), .out_3(out_3[7]));
endmodule

module enable (
  input  [7:0] in_1,
  input  in_2,
  output [7:0] out_3
);

  assign out_3 = in_2 ? in_1 : 8'bz;  // Controlled_Buffer controlled_buffer_1
endmodule

module registradorsetenable (
  input  [7:0] in_1,
  input  in_2,
  input  in_3,
  output [7:0] out_4
);

  wire [7:0] registrador_1_out_3;

  registrador registrador_1 (.in_1(in_1), .in_2(in_2), .out_3(registrador_1_out_3));
  enable enable_1 (.in_1(registrador_1_out_3), .in_2(in_3), .out_3(out_4));
endmodule

module decoder_2x4 (
  input  in_1,
  input  in_2,
  output out_3,
  output out_4,
  output out_5,
  output out_6
);

  wire not_1_out, not_2_out;

  not not_1 (not_1_out, in_1);
  not not_2 (not_2_out, in_2);
  and and_1 (out_3, not_1_out, not_2_out);
  and and_2 (out_4, in_1, not_2_out);
  and and_3 (out_5, not_1_out, in_2);
  and and_4 (out_6, in_1, in_2);
endmodule

module memory_16bit (
  input  [7:0] in_1,
  input  we,
  input  oe,
  input  [7:0] in_4,
  output [7:0] out_5
);

  wire and_1_out, and_2_out, and_3_out, decoder_1_out0, decoder_2_out0;

  Decoder #(.select(4)) decoder_1 (
    .out0(decoder_1_out0), .sel(in_1[7:4]));  // open: out1, out2, out3, out4, out5, out6, out7, out8, out9, out10, out11, out12, out13, out14, out15, en
  Decoder #(.select(4)) decoder_2 (
    .out0(decoder_2_out0), .sel(in_1[3:0]));  // open: out1, out2, out3, out4, out5, out6, out7, out8, out9, out10, out11, out12, out13, out14, out15, en
  and and_1 (and_1_out, decoder_2_out0, decoder_1_out0);
  and and_2 (and_2_out, and_1_out, we);
  registradorsetenable registradorsetenable_1 (.in_1(in_4), .in_2(and_2_out), .in_3(and_3_out), .out_4(out_5));
  and and_3 (and_3_out, and_1_out, oe);
endmodule

module shift_right (
  input  in_1,
  input  [7:0] in_2,
  output [7:0] out_3,
  output out_4
);


  assign out_3 = {in_1, in_2[7:1]};
  assign out_4 = in_2[0];
endmodule

module ula (
  input  in_1,
  input  [7:0] in_2,
  input  [7:0] in_3,
  input  in_4,
  input  in_5,
  output [7:0] out_6,
  output out_7,
  output [7:0] out_8,
  output out_9,
  output [7:0] out_10,
  output out_11
);

  Adder adder_1 (.a(in_2), .b(in_3), .out(out_6), .cin(in_1), .cout(out_7));
  shift_right shift_right_1 (.in_2(in_3), .in_1(in_4), .out_4(out_9), .out_3(out_8));
  shl shl_1 (.in_2(in_2), .in_1(in_5), .out_4(out_11), .out_3(out_10));
endmodule

module shl (
  input  in_1,
  input  [7:0] in_2,
  output [7:0] out_3,
  output out_4
);


  assign out_3 = {in_2[6:0], in_1};
  assign out_4 = in_2[7];
endmodule
